// Logisim project ArquiteturaDeComputadores.circ as structural Verilog
module Add1 (
  input  A,
  input  B,
  input  CARRY_IN,
  output S,
  output CARRY_OUT
);

  wire and_1_out, and_2_out, or_1_out, xor_1_out;

  xor xor_1 (xor_1_out, A, B);
  or or_1 (or_1_out, B, CARRY_IN);
  xor xor_2 (S, xor_1_out, CARRY_IN);
  and and_1 (and_1_out, B, CARRY_IN);
  and and_2 (and_2_out, or_1_out, A);
  or or_2 (CARRY_OUT, and_2_out, and_1_out);
endmodule

module Add4 (
  input  [3:0] A,
  input  [3:0] B,
  input  CARRY_IN,
  output OVERFLOW,
  output [3:0] SOMA
);

  wire add1_1_carry_out, add1_3_carry_out, add1_4_carry_out;

  Add1 add1_1 (.A(A[2]), .B(B[2]), .CARRY_IN(add1_3_carry_out), .S(SOMA[2]), .CARRY_OUT(add1_1_carry_out));
  Add1 add1_2 (.A(A[3]), .B(B[3]), .CARRY_IN(add1_1_carry_out), .S(SOMA[3]), .CARRY_OUT(OVERFLOW));
  Add1 add1_3 (.A(A[1]), .B(B[1]), .CARRY_IN(add1_4_carry_out), .S(SOMA[1]), .CARRY_OUT(add1_3_carry_out));
  Add1 add1_4 (.A(A[0]), .B(B[0]), .CARRY_IN(CARRY_IN), .S(SOMA[0]), .CARRY_OUT(add1_4_carry_out));
endmodule
